# Fritzing sketch schematic (saved by Fritzing 0.9.3b)

parts:
  KY-1 = Keyes Relay [package=THT]
  Raspberry_Pi_B_rev1 = Raspberry Pi B rev1
  R1 = Resistor [tolerance=±5% resistance=220 package=THT]
  R2 = Resistor [tolerance=±5% resistance=220 package=THT]
  DS1 = DS18B20 1-Wire Temperature Sensor [part_number=DS18B20]
  LCD1 = LCD screen
  LCM1602_IIC1 = LCM1602 IIC [part_number="LCM1602 IIC" chip_label="LCM1602 IIC" package="DIP (Dual Inline) [THT]"]
  S1 = Toggle Switch [package=THT]
  LED2 = LED - 3mm [color="Red (633nm)" package="3 mm [THT]"]

nets:
  5V: KY-1.signal, Raspberry_Pi_B_rev1.5V, LCM1602_IIC1.VCC
  N1: KY-1.power, Raspberry_Pi_B_rev1.GPIO_18
  GND: KY-1.ground, Raspberry_Pi_B_rev1.GND, DS1.GND, LCM1602_IIC1.GND, LED2.anode
  N2: Raspberry_Pi_B_rev1.3V3, R1.Pin_1
  N3: Raspberry_Pi_B_rev1.GPIO_0, LCM1602_IIC1.SDA
  N4: Raspberry_Pi_B_rev1.GPIO_1, LCM1602_IIC1.SCL
  N5: Raspberry_Pi_B_rev1.GPIO_17, R2.Pin_1
  N6: R1.Pin_0, DS1.DQ
  N7: R2.Pin_0, LED2.cathode
  VSS: LCD1.VSS, LCM1602_IIC1.VSS
  VDD: LCD1.VDD, LCM1602_IIC1.VDD
  N8: LCD1.V0, LCM1602_IIC1.V0
  N9: LCD1.RS, LCM1602_IIC1.RS
  N10: LCD1.R/W, LCM1602_IIC1.RW
  N11: LCD1.E, LCM1602_IIC1.E
  N12: LCD1.DB0, LCM1602_IIC1.D0
  N13: LCD1.DB1, LCM1602_IIC1.D1
  N14: LCD1.DB2, LCM1602_IIC1.D2
  N15: LCD1.DB3, LCM1602_IIC1.D3
  N16: LCD1.DB4, LCM1602_IIC1.D4
  N17: LCD1.DB5, LCM1602_IIC1.D5
  N18: LCD1.DB6, LCM1602_IIC1.D6
  N19: LCD1.DB7, LCM1602_IIC1.D7
  N20: LCD1.LED+, LCM1602_IIC1.A
  N21: LCD1.LED-, LCM1602_IIC1.K
  N22: LCM1602_IIC1.LED_A, S1.COM
  N23: LCM1602_IIC1.LED_B, S1.L1

custom parts:
  Keyes Relay: The Keyes 5V relay module is suitable for SCM development, home appliance control. It uses a 5V~12V TIL control signal which can control DC / AC signal.
  LCM1602 IIC: I2C-Module to use a 1602 or 2004 LCD on with the wire.h libory Serial LCD Modul
